# Fritzing sketch PCBtest (saved by Fritzing 0.9.3b)
circuit board: 10.7774cm x 7.14057cm
perfboards: 1

parts:
  IC14 = IC, DIP package, 14 pins [chip_label=CD4013]
  IC15 = IC, DIP package, 14 pins [chip_label=CD4013]
  IC16 = IC, DIP package, 14 pins [chip_label=CD4013]
  IC17 = IC, DIP package, 14 pins [chip_label=CD4013]
  IC18 = IC, DIP package, 14 pins [chip_label=CD4013]
  IC19 = IC, DIP package, 14 pins [chip_label=CD4013]
  IC20 = IC, DIP package, 14 pins [chip_label=CD4013]
  IC21 = IC, DIP package, 14 pins [chip_label=CD4013]
  J11 = double row male pin header, 4 pins [form="♂ (male)"]
  J12 = double row male pin header, 4 pins [form="♂ (male)"]
  J13 = double row male pin header, 4 pins [form="♂ (male)"]
  J14 = double row male pin header, 4 pins [form="♂ (male)"]
  J15 = double row male pin header, 4 pins [form="♂ (male)"]
  J16 = double row male pin header, 4 pins [form="♂ (male)"]
  J17 = double row male pin header, 4 pins [form="♂ (male)"]
  J19 = male pin header, 1 pin [form="♂ (male)"]
  Power4 = Generic male header - 2 pins [form="♂ (male)" package=THT]
  J18 = double row male pin header, 4 pins [form="♂ (male)"]

nets:
  N1: IC14.pin1, J15.pin3
  N2: IC14.pin3, IC14.pin11, IC15.pin3, IC15.pin11, IC16.pin3, IC16.pin11, IC17.pin3, IC17.pin11, IC18.pin3, IC18.pin11, IC19.pin3, IC19.pin11, IC20.pin3, IC20.pin11, IC21.pin3, IC21.pin11, J19.pin1
  N3: IC14.pin5, J11.pin3
  N4: IC14.pin7, IC15.pin7, IC16.pin7, IC17.pin7, IC18.pin7, IC19.pin7, IC20.pin7, IC21.pin7, Power4.GND
  N5: IC14.pin9, J11.pin4
  N6: IC14.pin13, J15.pin4
  N7: IC14.pin14, IC15.pin14, IC16.pin14, IC17.pin14, IC18.pin14, IC19.pin14, IC20.pin14, IC21.pin14, Power4.VCC
  N8: IC15.pin1, J15.pin1
  N9: IC15.pin5, J11.pin1
  N10: IC15.pin9, J11.pin2
  N11: IC15.pin13, J15.pin2
  N12: IC16.pin1, J16.pin3
  N13: IC16.pin5, J12.pin3
  N14: IC16.pin9, J12.pin4
  N15: IC16.pin13, J16.pin4
  N16: IC17.pin1, J16.pin1
  N17: IC17.pin5, J12.pin1
  N18: IC17.pin9, J12.pin2
  N19: IC17.pin13, J16.pin2
  N20: IC18.pin1, J17.pin3
  N21: IC18.pin5, J13.pin3
  N22: IC18.pin9, J13.pin4
  N23: IC18.pin13, J17.pin4
  N24: IC19.pin1, J17.pin1
  N25: IC19.pin5, J13.pin1
  N26: IC19.pin9, J13.pin2
  N27: IC19.pin13, J17.pin2
  N28: IC20.pin1, J18.pin3
  N29: IC20.pin5, J14.pin3
  N30: IC20.pin9, J14.pin4
  N31: IC20.pin13, J18.pin4
  N32: IC21.pin1, J18.pin1
  N33: IC21.pin5, J14.pin1
  N34: IC21.pin9, J14.pin2
  N35: IC21.pin13, J18.pin2

notes:
  RegCard
  OUTPUT
  INPUT

custom parts:
  Generic male header - 2 pins: Generic male header
