# Fritzing sketch gaaaaaaaaaanzschwierig (saved by Fritzing 0.9.3b)
circuit board: 40.1932cm x 21.1176cm
perfboards: 4

parts:
  IC2 = IC, DIP package, 28 pins [chip_label=CY62256]
  IC3 = IC, DIP package, 28 pins [chip_label=CY62256]
  IC4 = IC, DIP package, 28 pins [chip_label=CY62256]
  Adresse = longpad pin header, 10 pins [form="long pad"]
  Control = male pin header, 3 pins [form="♂ (male)"]
  Power = Generic male header - 2 pins [form="♂ (male)" package=THT]
  I/O = male pin header, 32 pins [form="♂ (male)"]
  IC1 = IC, DIP package, 28 pins [chip_label=CY62256]
  Power1 = Generic male header - 2 pins [form="♂ (male)" package=THT]  # not connected
  74LS181 = IC, DIP package, 24 pins [chip_label=74LS181]  # not connected
  J1 = double row male pin header, 4 pins [form="♂ (male)"]  # not connected
  Power2 = Generic male header - 2 pins [form="♂ (male)" package=THT]  # not connected
  IC5 = IC, DIP package, 16 pins [chip_label=CD4052]  # not connected
  IC6 = IC, DIP package, 14 pins [chip_label=CD4013]
  J2 = double row male pin header, 4 pins [form="♂ (male)"]
  IC7 = IC, DIP package, 14 pins [chip_label=CD4013]
  Power3 = Generic male header - 2 pins [form="♂ (male)" package=THT]
  J3 = male pin header, 1 pin [form="♂ (male)"]
  IC8 = IC, DIP package, 14 pins [chip_label=CD4013]
  IC9 = IC, DIP package, 14 pins [chip_label=CD4013]
  IC10 = IC, DIP package, 14 pins [chip_label=CD4013]
  IC11 = IC, DIP package, 14 pins [chip_label=CD4013]
  IC12 = IC, DIP package, 14 pins [chip_label=CD4013]
  IC13 = IC, DIP package, 14 pins [chip_label=CD4013]
  J4 = double row male pin header, 4 pins [form="♂ (male)"]
  J5 = double row male pin header, 4 pins [form="♂ (male)"]
  J6 = double row male pin header, 4 pins [form="♂ (male)"]
  J7 = double row male pin header, 4 pins [form="♂ (male)"]
  J8 = double row male pin header, 4 pins [form="♂ (male)"]

nets:
  N1: IC2.pin11, I/O.pin9
  N2: IC2.pin12, I/O.pin10
  N3: IC2.pin13, I/O.pin11
  N4: IC2.pin14, IC3.pin14, IC4.pin14, Power.GND, IC1.pin14
  N5: IC2.pin15, I/O.pin12
  N6: IC2.pin16, I/O.pin13
  N7: IC2.pin17, I/O.pin14
  N8: IC2.pin18, I/O.pin15
  N9: IC2.pin19, I/O.pin16
  N10: IC2.pin28, IC3.pin28, IC4.pin28, Power.VCC, IC1.pin28
  N11: IC3.pin11, I/O.pin17
  N12: IC3.pin12, I/O.pin18
  N13: IC3.pin13, I/O.pin19
  N14: IC3.pin15, I/O.pin20
  N15: IC3.pin16, I/O.pin21
  N16: IC3.pin17, I/O.pin22
  N17: IC3.pin18, I/O.pin23
  N18: IC3.pin19, I/O.pin24
  N19: IC4.pin11, I/O.pin25
  N20: IC4.pin12, I/O.pin26
  N21: IC4.pin13, I/O.pin27
  N22: IC4.pin15, I/O.pin28
  N23: IC4.pin16, I/O.pin29
  N24: IC4.pin17, I/O.pin30
  N25: IC4.pin18, I/O.pin31
  N26: IC4.pin19, I/O.pin32
  N27: IC4.pin20, Control.pin3
  N28: IC4.pin22, Control.pin2, IC1.pin22
  N29: IC4.pin27, Control.pin1, IC1.pin27
  N30: Adresse.pin1, IC1.pin21
  N31: Adresse.pin2, IC1.pin23
  N32: Adresse.pin3, IC1.pin24
  N33: Adresse.pin4, IC1.pin25
  N34: Adresse.pin5, IC1.pin26
  N35: Adresse.pin6, IC1.pin1
  N36: Adresse.pin7, IC1.pin2
  N37: Adresse.pin8, IC1.pin3
  N38: Adresse.pin9, IC1.pin4
  N39: Adresse.pin10, IC1.pin5
  N40: I/O.pin1, IC1.pin11
  N41: I/O.pin2, IC1.pin12
  N42: I/O.pin3, IC1.pin13
  N43: I/O.pin4, IC1.pin15
  N44: I/O.pin5, IC1.pin16
  N45: I/O.pin6, IC1.pin17
  N46: I/O.pin7, IC1.pin18
  N47: I/O.pin8, IC1.pin19
  N48: IC6.pin1, J2.pin1
  N49: IC6.pin5, J5.pin1
  N50: IC6.pin7, IC7.pin7, Power3.GND
  N51: IC6.pin9, J5.pin2
  N52: IC6.pin11, J3.pin1, IC12.pin3, IC13.pin3
  N53: IC6.pin13, J2.pin2
  N54: IC6.pin14, IC7.pin14, Power3.VCC
  N55: J2.pin3, IC7.pin1
  N56: J2.pin4, IC7.pin13
  N57: IC7.pin5, J5.pin3
  N58: IC7.pin9, J5.pin4
  N59: IC8.pin1, J4.pin1
  N60: IC8.pin5, J6.pin1
  N61: IC8.pin9, J6.pin2
  N62: IC8.pin13, J4.pin2
  N63: IC9.pin1, J4.pin3
  N64: IC9.pin5, J6.pin3
  N65: IC9.pin9, J6.pin4
  N66: IC9.pin13, J4.pin4
  N67: IC10.pin5, J7.pin1
  N68: IC10.pin9, J7.pin2
  N69: IC11.pin5, J7.pin3
  N70: IC11.pin9, J7.pin4
  N71: IC12.pin5, J8.pin1
  N72: IC12.pin9, J8.pin2
  N73: IC13.pin5, J8.pin3
  N74: IC13.pin9, J8.pin4

notes:
  MemoryCard
  ALUCard
  MUXCard

custom parts:
  Generic male header - 2 pins: Generic male header
