// Logisim project quicksketch10092020.circ as structural Verilog: 1 circuit, main circuit main
module main (
  input  in_1,
  input  [7:0] in_2,
  input  [1:0] in_3,
  input  in_4
);

  wire d_ff_1_q, d_ff_2_q, d_ff_3_q, demultiplexer_1_out0, demultiplexer_1_out1, demultiplexer_1_out2,
       demultiplexer_1_out3;
  wire [7:0] multiplexer_1_out, ram_1_data, undriven;

  RAM ram_1 (.addr(in_2), .data(ram_1_data));  // open: sel, clk, ld, clr
  Multiplexer #(.width(8), .enable("false")) multiplexer_1 (
    .in0(undriven), .in1(ram_1_data), .out(multiplexer_1_out), .sel(in_1));
  Demultiplexer #(.select(2), .enable("false")) demultiplexer_1 (
    .out0(demultiplexer_1_out0), .out1(demultiplexer_1_out1), .out2(demultiplexer_1_out2),
    .out3(demultiplexer_1_out3), .in(in_4), .sel(in_3));
  D_Flip_Flop d_ff_1 (
    .clk(demultiplexer_1_out0), .D(multiplexer_1_out[7]), .Q(d_ff_1_q));  // open: Qn, preset, en, reset
  D_Flip_Flop d_ff_2 (
    .clk(demultiplexer_1_out1), .D(multiplexer_1_out[7]), .Q(d_ff_2_q));  // open: Qn, preset, en, reset
  D_Flip_Flop d_ff_3 (
    .clk(demultiplexer_1_out2), .D(multiplexer_1_out[7]), .Q(d_ff_3_q));  // open: Qn, preset, en, reset
  D_Flip_Flop d_ff_4 (.clk(demultiplexer_1_out3), .D(multiplexer_1_out[7]));  // open: Q, Qn, preset, en, reset
  D_Flip_Flop d_ff_5 (.clk(demultiplexer_1_out0), .D(multiplexer_1_out[6]));  // open: Q, Qn, preset, en, reset
  D_Flip_Flop d_ff_6 (.clk(demultiplexer_1_out1), .D(multiplexer_1_out[6]));  // open: Q, Qn, preset, en, reset
  D_Flip_Flop d_ff_7 (.clk(demultiplexer_1_out2), .D(multiplexer_1_out[6]));  // open: Q, Qn, preset, en, reset
  D_Flip_Flop d_ff_8 (.clk(demultiplexer_1_out3), .D(multiplexer_1_out[6]));  // open: Q, Qn, preset, en, reset
  D_Flip_Flop d_ff_9 (.clk(demultiplexer_1_out0), .D(multiplexer_1_out[5]));  // open: Q, Qn, preset, en, reset
  D_Flip_Flop d_ff_10 (.clk(demultiplexer_1_out1), .D(multiplexer_1_out[5]));  // open: Q, Qn, preset, en, reset
  D_Flip_Flop d_ff_11 (.clk(demultiplexer_1_out2), .D(multiplexer_1_out[5]));  // open: Q, Qn, preset, en, reset
  D_Flip_Flop d_ff_12 (.clk(demultiplexer_1_out3), .D(multiplexer_1_out[5]));  // open: Q, Qn, preset, en, reset
  D_Flip_Flop d_ff_13 (.clk(demultiplexer_1_out0), .D(multiplexer_1_out[4]));  // open: Q, Qn, preset, en, reset
  D_Flip_Flop d_ff_14 (.clk(demultiplexer_1_out1), .D(multiplexer_1_out[4]));  // open: Q, Qn, preset, en, reset
  D_Flip_Flop d_ff_15 (.clk(demultiplexer_1_out2), .D(multiplexer_1_out[4]));  // open: Q, Qn, preset, en, reset
  D_Flip_Flop d_ff_16 (.clk(demultiplexer_1_out3), .D(multiplexer_1_out[4]));  // open: Q, Qn, preset, en, reset
  D_Flip_Flop d_ff_17 (.clk(demultiplexer_1_out0), .D(multiplexer_1_out[3]));  // open: Q, Qn, preset, en, reset
  D_Flip_Flop d_ff_18 (.clk(demultiplexer_1_out1), .D(multiplexer_1_out[3]));  // open: Q, Qn, preset, en, reset
  D_Flip_Flop d_ff_19 (.clk(demultiplexer_1_out2), .D(multiplexer_1_out[3]));  // open: Q, Qn, preset, en, reset
  D_Flip_Flop d_ff_20 (.clk(demultiplexer_1_out3), .D(multiplexer_1_out[3]));  // open: Q, Qn, preset, en, reset
  D_Flip_Flop d_ff_21 (.clk(demultiplexer_1_out0), .D(multiplexer_1_out[2]));  // open: Q, Qn, preset, en, reset
  D_Flip_Flop d_ff_22 (.clk(demultiplexer_1_out1), .D(multiplexer_1_out[2]));  // open: Q, Qn, preset, en, reset
  D_Flip_Flop d_ff_23 (.clk(demultiplexer_1_out2), .D(multiplexer_1_out[2]));  // open: Q, Qn, preset, en, reset
  D_Flip_Flop d_ff_24 (.clk(demultiplexer_1_out3), .D(multiplexer_1_out[2]));  // open: Q, Qn, preset, en, reset
  D_Flip_Flop d_ff_25 (.clk(demultiplexer_1_out0), .D(multiplexer_1_out[1]));  // open: Q, Qn, preset, en, reset
  D_Flip_Flop d_ff_26 (.clk(demultiplexer_1_out1), .D(multiplexer_1_out[1]));  // open: Q, Qn, preset, en, reset
  D_Flip_Flop d_ff_27 (.clk(demultiplexer_1_out2), .D(multiplexer_1_out[1]));  // open: Q, Qn, preset, en, reset
  D_Flip_Flop d_ff_28 (.clk(demultiplexer_1_out3), .D(multiplexer_1_out[1]));  // open: Q, Qn, preset, en, reset
  D_Flip_Flop d_ff_29 (.clk(demultiplexer_1_out0), .D(multiplexer_1_out[0]));  // open: Q, Qn, preset, en, reset
  D_Flip_Flop d_ff_30 (.clk(demultiplexer_1_out1), .D(multiplexer_1_out[0]));  // open: Q, Qn, preset, en, reset
  D_Flip_Flop d_ff_31 (.clk(demultiplexer_1_out2), .D(multiplexer_1_out[0]));  // open: Q, Qn, preset, en, reset
  D_Flip_Flop d_ff_32 (.clk(demultiplexer_1_out3), .D(multiplexer_1_out[0]));  // open: Q, Qn, preset, en, reset
endmodule
