// Logisim project quicktest10042020.circ as structural Verilog: 1 circuit, main circuit main
module main (
  input  [7:0] in_1,
  input  in_2,
  input  in_3
);

  wire not_1_out, not_2_out, pull_resistor_2_node, pull_resistor_3_node, pull_resistor_5_node,
       pull_resistor_6_node, pull_resistor_7_node, undriven;
  wire [7:0] adder_1_out, controlled_buffer_1_out, controlled_buffer_4_out, controlled_buffer_5_out,
       demultiplexer_1_out0, demultiplexer_1_out1, demultiplexer_1_out2, demultiplexer_1_out3,
       demultiplexer_1_out4, demultiplexer_1_out5, demultiplexer_1_out6, demultiplexer_1_out7,
       Instruktionsregister_q, multiplexer_1_out, multiplexer_3_out, pull_resistor_1_node,
       pull_resistor_4_node, pull_resistor_8_node, ram_1_data, register_1_q, register_2_q, register_3_q,
       register_4_q, register_5_q;
  wire [31:0] multiplexer_2_out;

  Pull_Resistor pull_resistor_1 (.node(pull_resistor_1_node));
  Pull_Resistor #(.pull(1)) pull_resistor_2 (.node(pull_resistor_2_node));
  Adder adder_1 (
    .a(register_1_q), .b(pull_resistor_1_node), .out(adder_1_out), .cin(pull_resistor_2_node));  // open: cout
  RAM ram_1 (.addr(register_1_q), .data(ram_1_data), .clk(in_2), .ld(not_1_out));  // open: sel, clr
  not not_1 (not_1_out, pull_resistor_3_node);
  Pull_Resistor pull_resistor_3 (.node(pull_resistor_3_node));
  Multiplexer #(.width(8), .disabled(0), .enable("false")) multiplexer_1 (
    .in0(adder_1_out), .in1(controlled_buffer_5_out), .out(multiplexer_1_out), .sel(pull_resistor_7_node));
  Register register_1 (.D(multiplexer_1_out), .Q(register_1_q), .clk(in_3));  // open: en, clr
  assign controlled_buffer_1_out = not_1_out ? ram_1_data : 8'bz;  // Controlled_Buffer controlled_buffer_1
  assign ram_1_data = pull_resistor_3_node ? in_1 : 8'bz;  // Controlled_Buffer controlled_buffer_2
  Pull_Resistor pull_resistor_4 (.node(pull_resistor_4_node));
  assign pull_resistor_4_node = pull_resistor_6_node ? pull_resistor_8_node : 8'bz;  // Controlled_Buffer ALU_Return
  assign pull_resistor_4_node = pull_resistor_5_node ? controlled_buffer_1_out : 8'bz;  // Controlled_Buffer controlled_buffer_3
  assign controlled_buffer_4_out = not_2_out ? controlled_buffer_1_out : 8'bz;  // Controlled_Buffer controlled_buffer_4
  not not_2 (not_2_out, pull_resistor_5_node);
  Pull_Resistor pull_resistor_5 (.node(pull_resistor_5_node));
  assign controlled_buffer_5_out = pull_resistor_7_node ? controlled_buffer_1_out : 8'bz;  // Controlled_Buffer controlled_buffer_5
  Pull_Resistor pull_resistor_6 (.node(pull_resistor_6_node));
  Pull_Resistor pull_resistor_7 (.node(pull_resistor_7_node));
  Pull_Resistor pull_resistor_8 (.node(pull_resistor_8_node));
  Register Instruktionsregister (.D(controlled_buffer_4_out), .Q(Instruktionsregister_q));  // open: en, clk, clr
  Demultiplexer #(.select(3), .width(8), .enable("false")) demultiplexer_1 (
    .out0(demultiplexer_1_out0), .out1(demultiplexer_1_out1), .out2(demultiplexer_1_out2),
    .out3(demultiplexer_1_out3), .out4(demultiplexer_1_out4), .out5(demultiplexer_1_out5),
    .out6(demultiplexer_1_out6), .out7(demultiplexer_1_out7), .in(pull_resistor_4_node),
    .sel(Instruktionsregister_q[6:4]));
  Multiplexer #(.select(4), .width(32), .disabled(0), .enable("false")) multiplexer_2 (
    .out(multiplexer_2_out), .sel(Instruktionsregister_q[3:0]));  // open: in0, in1, in2, in3, in4, in5, in6, in7, in8, in9, in10, in11, in12, in13, in14, in15
  Register register_2 (.D(demultiplexer_1_out0), .Q(register_2_q), .clk(undriven));  // open: en, clr
  Register register_3 (.D(demultiplexer_1_out1), .Q(register_3_q), .clk(undriven));  // open: en, clr
  Register register_4 (.D(demultiplexer_1_out2), .Q(register_4_q), .clk(undriven));  // open: en, clr
  Register register_5 (.D(demultiplexer_1_out3), .Q(register_5_q), .clk(undriven));  // open: en, clr
  Register register_6 (.D(demultiplexer_1_out4), .clk(undriven));  // open: en, Q, clr
  Register register_7 (.D(demultiplexer_1_out5), .clk(undriven));  // open: en, Q, clr
  Register register_8 (.D(demultiplexer_1_out6), .clk(undriven));  // open: en, Q, clr
  Register register_9 (.D(demultiplexer_1_out7), .Q(in_1), .clk(undriven));  // open: en, clr
  Multiplexer #(.select(3), .width(8), .enable("false")) multiplexer_3 (.out(multiplexer_3_out));  // open: in0, in1, in2, in3, in4, in5, in6, in7, sel

  // Notes on the sheet:
  //   spezielle anweisung
  //   64bit fehlt!!!
  //   Schreibflag
  //   Speicherregister
  //   Datenflag
  //   von ALU
  //   ALU DATA FLAG
  //   Befehlsdecoder
  //   ____
  //   ausarbeiten!
  //   Registerauswahl
  //   Prozessorrelevante Flags und Anweisung zur Befehlsausfuehrung
  //   Datenregister
  //   zu ALU
  //   ALUin 1
endmodule
