// Logisim project quicktest11112020withTMUandIPCidea.circ as structural Verilog
module main (
  input  CLK,
  input  RESET
);

  wire comparator_1_eq, comparator_1_gt, comparator_1_lt, not_1_out, time_management_unit_1_clk_adr,
       time_management_unit_1_clk_ins, time_management_unit_1_clk_ld, time_management_unit_1_write, undriven,
       undriven_3;
  wire [1:0] undriven_2;
  wire [7:0] adder_1_out, adder_2_out, demultiplexer_1_out0, demultiplexer_1_out1, multiplexer_1_out,
       multiplexer_2_out, multiplexer_3_out, multiplexer_4_out, ram_1_data, register_1_q, register_2_q,
       register_3_q, register_4_q;

  Adder adder_1 (.a(register_1_q), .b({8{1'b0}}), .out(adder_1_out), .cin(1'b1));  // open: cout
  Multiplexer #(.width(8), .enable("false")) multiplexer_1 (
    .in0(adder_1_out), .in1(multiplexer_4_out), .out(multiplexer_1_out), .sel(register_2_q[0]));
  Register register_1 (
    .D(multiplexer_1_out), .Q(register_1_q), .clk(time_management_unit_1_clk_adr), .clr(RESET));  // open: en
  not not_1 (not_1_out, time_management_unit_1_write);
  RAM #(.bus("asynch")) ram_1 (.addr(register_1_q), .data(ram_1_data), .ld(not_1_out));  // open: sel, clr
  Pull_Resistor pull_resistor_1 (.node(ram_1_data));
  assign ram_1_data = register_2_q[3] ? adder_2_out : 8'bz;  // Controlled_Buffer controlled_buffer_1
  Demultiplexer #(.width(8), .enable("false")) demultiplexer_1 (
    .out0(demultiplexer_1_out0), .out1(demultiplexer_1_out1), .in(multiplexer_2_out), .sel(undriven));
  Multiplexer #(.width(8), .enable("false")) multiplexer_2 (
    .in0(adder_2_out), .in1(ram_1_data), .out(multiplexer_2_out), .sel(register_2_q[4]));
  Register register_2 (.D(ram_1_data), .Q(register_2_q), .clk(time_management_unit_1_clk_ins));  // open: en, clr
  Time_Management_Unit time_management_unit_1 (
    .loadflag(register_2_q[7]), .aluflag(register_2_q[4]), .writeflag(register_2_q[2]),
    .CLK_INS(time_management_unit_1_clk_ins), .CLK_ADR(time_management_unit_1_clk_adr),
    .CLK_LD(time_management_unit_1_clk_ld), .WRITE(time_management_unit_1_write), .CLK(CLK), .RESET(RESET));
  Register register_3 (
    .D(demultiplexer_1_out0), .Q(register_3_q), .clk(time_management_unit_1_clk_ld));  // open: en, clr
  Register register_4 (
    .D(demultiplexer_1_out1), .Q(register_4_q), .clk(time_management_unit_1_clk_ld));  // open: en, clr
  Multiplexer #(.width(8), .enable("false")) multiplexer_3 (
    .in0(register_3_q), .in1(register_4_q), .out(multiplexer_3_out), .sel(register_2_q[6]));
  Multiplexer #(.width(8), .enable("false")) multiplexer_4 (
    .in0(register_3_q), .in1(register_4_q), .out(multiplexer_4_out), .sel(register_2_q[5]));
  Adder adder_2 (.a(multiplexer_4_out), .b(multiplexer_3_out), .out(adder_2_out));  // open: cin, cout
  Comparator comparator_1 (
    .a(multiplexer_4_out), .b(multiplexer_3_out), .gt(comparator_1_gt), .eq(comparator_1_eq),
    .lt(comparator_1_lt));
  Multiplexer #(.select(2)) multiplexer_5 (
    .in0(comparator_1_gt), .in1(comparator_1_eq), .in2(comparator_1_lt), .sel(undriven_2), .en(undriven_3));  // open: in3, out

  // Notes on the sheet:
  //   ADD IPC somewhere here
  //   JUMP Flag
  //   WRITE Flag
  //   WRITE Flag
  //   ALU Return Flag
  //   DEST
  //   DEMUX (for design with small memory width) here?
  //   SRC0
  //   SRC1
  //   ALU
  //   what holds the state of the ALU? -> Insert FlipFlop here somewhere
endmodule

module Time_Management_Unit (
  input  loadflag,
  input  aluflag,
  input  writeflag,
  input  CLK,
  input  RESET,
  output CLK_INS,
  output CLK_ADR,
  output CLK_LD,
  output WRITE
);

  wire demultiplexer_1_out0, demultiplexer_1_out2, demultiplexer_1_out3, not_1_out, or_1_out, register_1_q,
       register_3_q, xor_1_out;
  wire [1:0] counter_1_q;

  xor xor_1 (xor_1_out, CLK_LD, CLK_INS);
  Register #(.width(1)) register_1 (.D(or_1_out), .Q(register_1_q), .clk(xor_1_out));  // open: en, clr
  or or_1 (or_1_out, loadflag, aluflag);
  Register #(.width(1)) register_2 (.clk(xor_1_out));  // open: D, en, Q, clr
  Register #(.width(1)) register_3 (.D(writeflag), .Q(register_3_q), .clk(xor_1_out));  // open: en, clr
  Counter #(.width(2), .max('h3)) counter_1 (.Q(counter_1_q), .clk(CLK), .clr(RESET));  // open: load, D, count, carry
  Demultiplexer #(.select(2), .enable("false")) demultiplexer_1 (
    .out0(demultiplexer_1_out0), .out1(CLK_ADR), .out2(demultiplexer_1_out2), .out3(demultiplexer_1_out3),
    .in(1'b1), .sel(counter_1_q));
  and and_1 (CLK_INS, not_1_out, demultiplexer_1_out0);
  not not_1 (not_1_out, register_1_q);
  D_Flip_Flop d_ff_1 (
    .clk(CLK_ADR), .D(register_3_q), .Q(WRITE), .reset(demultiplexer_1_out3));  // open: Qn, preset, en
  and and_2 (CLK_LD, register_1_q, demultiplexer_1_out2);
endmodule

module neu (
  input  A,
  input  LF,
  output OUT
);

  wire not_1_out;

  not not_1 (not_1_out, LF);
  and and_1 (OUT, A, not_1_out);
endmodule

module TMUwithFLIPFLOP (
  input  loadflag,
  input  aluflag,
  input  writeflag,
  input  CLK,
  input  RESET,
  output CLK_INS,
  output CLK_ADR,
  output CLK_LD,
  output WRITE
);

  wire d_ff_1_q, d_ff_2_q, demultiplexer_1_out0, demultiplexer_1_out2, demultiplexer_1_out3, not_1_out,
       or_1_out, xor_1_out;
  wire [1:0] counter_1_q;

  xor xor_1 (xor_1_out, CLK_LD, CLK_INS);
  or or_1 (or_1_out, loadflag, aluflag);
  D_Flip_Flop d_ff_1 (.clk(xor_1_out), .D(or_1_out), .Q(d_ff_1_q));  // open: Qn, preset, en, reset
  D_Flip_Flop d_ff_2 (.clk(xor_1_out), .D(writeflag), .Q(d_ff_2_q));  // open: Qn, preset, en, reset
  Demultiplexer #(.select(2), .enable("false")) demultiplexer_1 (
    .out0(demultiplexer_1_out0), .out1(CLK_ADR), .out2(demultiplexer_1_out2), .out3(demultiplexer_1_out3),
    .in(1'b1), .sel(counter_1_q));
  Counter #(.width(2), .max('h3)) counter_1 (.Q(counter_1_q), .clk(CLK), .clr(RESET));  // open: load, D, count, carry
  and and_1 (CLK_INS, not_1_out, demultiplexer_1_out0);
  not not_1 (not_1_out, d_ff_1_q);
  D_Flip_Flop d_ff_3 (.clk(CLK_ADR), .D(d_ff_2_q), .Q(WRITE), .reset(demultiplexer_1_out3));  // open: Qn, preset, en
  and and_2 (CLK_LD, d_ff_1_q, demultiplexer_1_out2);

  // Notes on the sheet:
  //   Counter als IC
endmodule

module CD4013 (
  input  VDD,
  input  VSS,
  input  CLOCK1,
  input  D1,
  input  SET1,
  input  RESET1,
  input  CLOCK2,
  input  D2,
  input  SET2,
  input  RESET2,
  output Q1,
  output nQ1,
  output Q2,
  output nQ2
);

  D_Flip_Flop d_ff_1 (.clk(CLOCK1), .D(D1), .Q(Q1), .Qn(nQ1), .preset(SET1), .reset(RESET1));  // open: en
  D_Flip_Flop d_ff_2 (.clk(CLOCK2), .D(D2), .Q(Q2), .Qn(nQ2), .preset(SET2), .reset(RESET2));  // open: en
endmodule

module Group3 (
  input  [7:0] in_1
);

  wire cd4013_1_q1, cd4013_1_q2, cd4013_2_q1, cd4013_2_q2, cd4013_3_q2, cd4013_4_q2, cd4013_5_q1,
       cd4013_5_q2, cd4013_6_q1, cd4013_6_q2, cd4013_7_q2, cd4013_8_q2, cd4013_9_q1, cd4013_9_q2,
       cd4013_10_q1, cd4013_10_q2, cd4013_11_q2, cd4013_12_q2, cd4013_13_q1, cd4013_13_q2, cd4013_14_q1,
       cd4013_14_q2, cd4013_15_q2, cd4013_16_q2, cd4013_17_q1, cd4013_17_q2, cd4013_18_q1, cd4013_18_q2,
       cd4013_19_q2, cd4013_20_q2, cd4013_21_q1, cd4013_21_q2, cd4013_22_q1, cd4013_22_q2, cd4013_23_q2,
       cd4013_24_q2, cd4013_25_q1, cd4013_25_q2, cd4013_26_q1, cd4013_26_q2, cd4013_29_q1, cd4013_29_q2,
       cd4013_30_q1, cd4013_30_q2, undriven, undriven_2, undriven_3, undriven_4, undriven_5, undriven_6,
       undriven_7, undriven_8;

  CD4013 cd4013_1 (
    .CLOCK1(undriven_5), .D1(in_1[0]), .D2(in_1[1]), .Q1(cd4013_1_q1), .Q2(cd4013_1_q2));  // open: VDD, VSS, CLOCK2, nQ1, nQ2, SET1, SET2, RESET1, RESET2
  CD4013 cd4013_2 (
    .CLOCK1(undriven), .D1(in_1[0]), .D2(in_1[1]), .Q1(cd4013_2_q1), .Q2(cd4013_2_q2));  // open: VDD, VSS, CLOCK2, nQ1, nQ2, SET1, SET2, RESET1, RESET2
  CD4013 cd4013_3 (
    .CLOCK1(undriven_7), .D1(in_1[0]), .D2(in_1[1]), .Q2(cd4013_3_q2));  // open: VDD, VSS, CLOCK2, Q1, nQ1, nQ2, SET1, SET2, RESET1, RESET2
  CD4013 cd4013_4 (
    .CLOCK1(undriven_3), .D1(in_1[0]), .D2(in_1[1]), .Q2(cd4013_4_q2));  // open: VDD, VSS, CLOCK2, Q1, nQ1, nQ2, SET1, SET2, RESET1, RESET2
  CD4013 cd4013_5 (
    .CLOCK1(undriven_6), .D1(in_1[0]), .D2(in_1[1]), .Q1(cd4013_5_q1), .Q2(cd4013_5_q2));  // open: VDD, VSS, CLOCK2, nQ1, nQ2, SET1, SET2, RESET1, RESET2
  CD4013 cd4013_6 (
    .CLOCK1(undriven_2), .D1(in_1[0]), .D2(in_1[1]), .Q1(cd4013_6_q1), .Q2(cd4013_6_q2));  // open: VDD, VSS, CLOCK2, nQ1, nQ2, SET1, SET2, RESET1, RESET2
  CD4013 cd4013_7 (
    .CLOCK1(undriven_8), .D1(in_1[0]), .D2(in_1[1]), .Q2(cd4013_7_q2));  // open: VDD, VSS, CLOCK2, Q1, nQ1, nQ2, SET1, SET2, RESET1, RESET2
  CD4013 cd4013_8 (
    .CLOCK1(undriven_4), .D1(in_1[0]), .D2(in_1[1]), .Q2(cd4013_8_q2));  // open: VDD, VSS, CLOCK2, Q1, nQ1, nQ2, SET1, SET2, RESET1, RESET2
  CD4013 cd4013_9 (
    .CLOCK1(undriven_5), .D1(in_1[2]), .D2(in_1[3]), .Q1(cd4013_9_q1), .Q2(cd4013_9_q2));  // open: VDD, VSS, CLOCK2, nQ1, nQ2, SET1, SET2, RESET1, RESET2
  CD4013 cd4013_10 (
    .CLOCK1(undriven), .D1(in_1[2]), .D2(in_1[3]), .Q1(cd4013_10_q1), .Q2(cd4013_10_q2));  // open: VDD, VSS, CLOCK2, nQ1, nQ2, SET1, SET2, RESET1, RESET2
  CD4013 cd4013_11 (
    .CLOCK1(undriven_7), .D1(in_1[2]), .D2(in_1[3]), .Q2(cd4013_11_q2));  // open: VDD, VSS, CLOCK2, Q1, nQ1, nQ2, SET1, SET2, RESET1, RESET2
  CD4013 cd4013_12 (
    .CLOCK1(undriven_3), .D1(in_1[2]), .D2(in_1[3]), .Q2(cd4013_12_q2));  // open: VDD, VSS, CLOCK2, Q1, nQ1, nQ2, SET1, SET2, RESET1, RESET2
  CD4013 cd4013_13 (
    .CLOCK1(undriven_6), .D1(in_1[2]), .D2(in_1[3]), .Q1(cd4013_13_q1), .Q2(cd4013_13_q2));  // open: VDD, VSS, CLOCK2, nQ1, nQ2, SET1, SET2, RESET1, RESET2
  CD4013 cd4013_14 (
    .CLOCK1(undriven_2), .D1(in_1[2]), .D2(in_1[3]), .Q1(cd4013_14_q1), .Q2(cd4013_14_q2));  // open: VDD, VSS, CLOCK2, nQ1, nQ2, SET1, SET2, RESET1, RESET2
  CD4013 cd4013_15 (
    .CLOCK1(undriven_8), .D1(in_1[2]), .D2(in_1[3]), .Q2(cd4013_15_q2));  // open: VDD, VSS, CLOCK2, Q1, nQ1, nQ2, SET1, SET2, RESET1, RESET2
  CD4013 cd4013_16 (
    .CLOCK1(undriven_4), .D1(in_1[2]), .D2(in_1[3]), .Q2(cd4013_16_q2));  // open: VDD, VSS, CLOCK2, Q1, nQ1, nQ2, SET1, SET2, RESET1, RESET2
  CD4013 cd4013_17 (
    .CLOCK1(undriven_5), .D1(in_1[4]), .D2(in_1[5]), .Q1(cd4013_17_q1), .Q2(cd4013_17_q2));  // open: VDD, VSS, CLOCK2, nQ1, nQ2, SET1, SET2, RESET1, RESET2
  CD4013 cd4013_18 (
    .CLOCK1(undriven), .D1(in_1[4]), .D2(in_1[5]), .Q1(cd4013_18_q1), .Q2(cd4013_18_q2));  // open: VDD, VSS, CLOCK2, nQ1, nQ2, SET1, SET2, RESET1, RESET2
  CD4013 cd4013_19 (
    .CLOCK1(undriven_7), .D1(in_1[4]), .D2(in_1[5]), .Q2(cd4013_19_q2));  // open: VDD, VSS, CLOCK2, Q1, nQ1, nQ2, SET1, SET2, RESET1, RESET2
  CD4013 cd4013_20 (
    .CLOCK1(undriven_3), .D1(in_1[4]), .D2(in_1[5]), .Q2(cd4013_20_q2));  // open: VDD, VSS, CLOCK2, Q1, nQ1, nQ2, SET1, SET2, RESET1, RESET2
  CD4013 cd4013_21 (
    .CLOCK1(undriven_6), .D1(in_1[4]), .D2(in_1[5]), .Q1(cd4013_21_q1), .Q2(cd4013_21_q2));  // open: VDD, VSS, CLOCK2, nQ1, nQ2, SET1, SET2, RESET1, RESET2
  CD4013 cd4013_22 (
    .CLOCK1(undriven_2), .D1(in_1[4]), .D2(in_1[5]), .Q1(cd4013_22_q1), .Q2(cd4013_22_q2));  // open: VDD, VSS, CLOCK2, nQ1, nQ2, SET1, SET2, RESET1, RESET2
  CD4013 cd4013_23 (
    .CLOCK1(undriven_8), .D1(in_1[4]), .D2(in_1[5]), .Q2(cd4013_23_q2));  // open: VDD, VSS, CLOCK2, Q1, nQ1, nQ2, SET1, SET2, RESET1, RESET2
  CD4013 cd4013_24 (
    .CLOCK1(undriven_4), .D1(in_1[4]), .D2(in_1[5]), .Q2(cd4013_24_q2));  // open: VDD, VSS, CLOCK2, Q1, nQ1, nQ2, SET1, SET2, RESET1, RESET2
  CD4013 cd4013_25 (
    .CLOCK1(undriven_5), .D1(in_1[6]), .D2(in_1[7]), .Q1(cd4013_25_q1), .Q2(cd4013_25_q2));  // open: VDD, VSS, CLOCK2, nQ1, nQ2, SET1, SET2, RESET1, RESET2
  CD4013 cd4013_26 (
    .CLOCK1(undriven), .D1(in_1[6]), .D2(in_1[7]), .Q1(cd4013_26_q1), .Q2(cd4013_26_q2));  // open: VDD, VSS, CLOCK2, nQ1, nQ2, SET1, SET2, RESET1, RESET2
  CD4013 cd4013_27 (
    .CLOCK1(undriven_7), .D1(in_1[6]), .D2(in_1[7]));  // open: VDD, VSS, CLOCK2, Q1, nQ1, Q2, nQ2, SET1, SET2, RESET1, RESET2
  CD4013 cd4013_28 (
    .CLOCK1(undriven_3), .D1(in_1[6]), .D2(in_1[7]));  // open: VDD, VSS, CLOCK2, Q1, nQ1, Q2, nQ2, SET1, SET2, RESET1, RESET2
  CD4013 cd4013_29 (
    .CLOCK1(undriven_6), .D1(in_1[6]), .D2(in_1[7]), .Q1(cd4013_29_q1), .Q2(cd4013_29_q2));  // open: VDD, VSS, CLOCK2, nQ1, nQ2, SET1, SET2, RESET1, RESET2
  CD4013 cd4013_30 (
    .CLOCK1(undriven_2), .D1(in_1[6]), .D2(in_1[7]), .Q1(cd4013_30_q1), .Q2(cd4013_30_q2));  // open: VDD, VSS, CLOCK2, nQ1, nQ2, SET1, SET2, RESET1, RESET2
  CD4013 cd4013_31 (
    .CLOCK1(undriven_8), .D1(in_1[6]), .D2(in_1[7]));  // open: VDD, VSS, CLOCK2, Q1, nQ1, Q2, nQ2, SET1, SET2, RESET1, RESET2
  CD4013 cd4013_32 (
    .CLOCK1(undriven_4), .D1(in_1[6]), .D2(in_1[7]));  // open: VDD, VSS, CLOCK2, Q1, nQ1, Q2, nQ2, SET1, SET2, RESET1, RESET2
endmodule
