// Logisim project quicktest22062020.circ as structural Verilog: 2 circuits, main circuit main
module main (
  input  [7:0] in_1,
  input  in_2,
  input  in_3,
  input  in_4
);

  wire not_1_out, not_2_out, pull_resistor_2_node, pull_resistor_3_node, undriven_2;
  wire [7:0] adder_1_out, controlled_buffer_1_out, controlled_buffer_4_out, controlled_buffer_5_out,
       demultiplexer_1_out0, demultiplexer_1_out1, demultiplexer_1_out2, demultiplexer_1_out3,
       demultiplexer_1_out4, demultiplexer_1_out5, demultiplexer_1_out6, demultiplexer_1_out7,
       Instruktionsregister_q, multiplexer_1_out, pull_resistor_1_node, pull_resistor_4_node, ram_1_data,
       register_1_q, register_2_q, register_3_q, register_4_q, register_5_q, register_6_q, register_7_q,
       register_8_q, register_9_q, undriven;
  wire [31:0] multiplexer_2_out;

  Pull_Resistor pull_resistor_1 (.node(pull_resistor_1_node));
  Pull_Resistor #(.pull(1)) pull_resistor_2 (.node(pull_resistor_2_node));
  Adder adder_1 (
    .a(register_1_q), .b(pull_resistor_1_node), .out(adder_1_out), .cin(pull_resistor_2_node));  // open: cout
  RAM ram_1 (.addr(register_1_q), .data(ram_1_data), .clk(in_3), .ld(not_1_out));  // open: sel, clr
  not not_1 (not_1_out, pull_resistor_3_node);
  Pull_Resistor pull_resistor_3 (.node(pull_resistor_3_node));
  Register register_1 (.D(multiplexer_1_out), .Q(register_1_q), .clk(in_4));  // open: en, clr
  Multiplexer #(.width(8), .disabled(0), .enable("false")) multiplexer_1 (
    .in0(adder_1_out), .in1(controlled_buffer_5_out), .out(multiplexer_1_out), .sel(multiplexer_2_out[1]));
  assign controlled_buffer_1_out = not_1_out ? ram_1_data : 8'bz;  // Controlled_Buffer controlled_buffer_1
  assign ram_1_data = pull_resistor_3_node ? in_1 : 8'bz;  // Controlled_Buffer controlled_buffer_2
  Pull_Resistor pull_resistor_4 (.node(pull_resistor_4_node));
  assign pull_resistor_4_node = multiplexer_2_out[0] ? undriven : 8'bz;  // Controlled_Buffer ALU_Return
  assign pull_resistor_4_node = multiplexer_2_out[3] ? controlled_buffer_1_out : 8'bz;  // Controlled_Buffer controlled_buffer_3
  assign controlled_buffer_4_out = not_2_out ? controlled_buffer_1_out : 8'bz;  // Controlled_Buffer controlled_buffer_4
  not not_2 (not_2_out, multiplexer_2_out[3]);
  assign controlled_buffer_5_out = multiplexer_2_out[1] ? controlled_buffer_1_out : 8'bz;  // Controlled_Buffer controlled_buffer_5
  Register Instruktionsregister (.D(controlled_buffer_4_out), .Q(Instruktionsregister_q), .clk(in_2));  // open: en, clr
  Demultiplexer #(.select(3), .width(8), .enable("false")) demultiplexer_1 (
    .out0(demultiplexer_1_out0), .out1(demultiplexer_1_out1), .out2(demultiplexer_1_out2),
    .out3(demultiplexer_1_out3), .out4(demultiplexer_1_out4), .out5(demultiplexer_1_out5),
    .out6(demultiplexer_1_out6), .out7(demultiplexer_1_out7), .in(pull_resistor_4_node),
    .sel(Instruktionsregister_q[6:4]));
  Multiplexer #(.select(4), .width(32), .disabled(0), .enable("false")) multiplexer_2 (
    .in0(32'h1), .in1(32'h2), .in2(32'h4), .in3(32'h8), .out(multiplexer_2_out),
    .sel(Instruktionsregister_q[3:0]));  // open: in4, in5, in6, in7, in8, in9, in10, in11, in12, in13, in14, in15
  Register register_2 (.D(demultiplexer_1_out0), .Q(register_2_q), .clk(undriven_2));  // open: en, clr
  Register register_3 (.D(demultiplexer_1_out1), .Q(register_3_q), .clk(undriven_2));  // open: en, clr
  Register register_4 (.D(demultiplexer_1_out2), .Q(register_4_q), .clk(undriven_2));  // open: en, clr
  Register register_5 (.D(demultiplexer_1_out3), .Q(register_5_q), .clk(undriven_2));  // open: en, clr
  Register register_6 (.D(demultiplexer_1_out4), .Q(register_6_q), .clk(undriven_2));  // open: en, clr
  Register register_7 (.D(demultiplexer_1_out5), .Q(register_7_q), .clk(undriven_2));  // open: en, clr
  Register register_8 (.D(demultiplexer_1_out6), .Q(register_8_q), .clk(undriven_2));  // open: en, clr
  Register register_9 (.D(demultiplexer_1_out7), .Q(register_9_q), .clk(undriven_2));  // open: en, clr
  Multiplexer #(.select(3), .width(8), .enable("false")) multiplexer_3 (
    .in0(register_2_q), .in1(register_3_q), .in2(register_4_q), .in3(register_5_q), .in4(register_6_q),
    .in5(register_7_q), .in6(register_8_q), .in7(register_9_q), .out(in_1));  // open: sel

  // Notes on the sheet:
  //   spezielle anweisung
  //   64bit fehlt!!!
  //   Schreibflag
  //   "Adresspuffer"
  //   Datenflag
  //   alternativadresse kann nicht direkt aus speicher kommen!!!
  //   jumpflag
  //   von ALU
  //   ALU DATA FLAG
  //   Befehlsdecoder
  //   ____
  //   ausarbeiten!
  //   Registerauswahl
  //   Prozessorrelevante Flags und Anweisung zur Befehlsausfuehrung
  //   Datenregister
  //   ??? Entweder ReturnRegister zu Speicher oder Registerauswahl
  //   ALUin 0
  //   zu ALU
  //   ALUin 1
endmodule

module Time_Management_Unit (
  input  preINS,
  input  postINS
);

  wire comparator_1_gt, comparator_1_lt, or_1_out;

  Comparator #(.width(1), .mode("unsigned")) comparator_1 (
    .a(preINS), .b(postINS), .gt(comparator_1_gt), .lt(comparator_1_lt));  // open: eq
  or or_1 (or_1_out, comparator_1_gt, comparator_1_lt);

  // Notes on the sheet:
  //   InsLoadRequest
  //   DatLoadRequest
endmodule
