// Logisim project quicktest02072020.circ as structural Verilog: 5 circuits, main circuit main
module main (
  input  [7:0] in_1,
  input  in_2,
  input  in_3,
  input  in_4,
  output ALUFLAG_A_B
);

  wire not_1_out, not_2_out, or_1_out, pull_resistor_2_node, pull_resistor_3_node, pull_resistor_5_node,
       undriven_2;
  wire [7:0] adder_1_out, controlled_buffer_1_out, controlled_buffer_4_out, controlled_buffer_5_out,
       demultiplexer_1_out0, demultiplexer_1_out1, demultiplexer_1_out2, demultiplexer_1_out3,
       demultiplexer_1_out4, demultiplexer_1_out5, demultiplexer_1_out6, demultiplexer_1_out7,
       Instruktionsregister_q, multiplexer_1_out, pull_resistor_1_node, pull_resistor_4_node, ram_1_data,
       register_1_q, register_2_q, register_3_q, register_4_q, register_5_q, register_6_q, register_7_q,
       register_8_q, register_9_q, Speicherregister_q, undriven, undriven_3;
  wire [31:0] multiplexer_2_out;

  Pull_Resistor pull_resistor_1 (.node(pull_resistor_1_node));
  Pull_Resistor #(.pull(1)) pull_resistor_2 (.node(pull_resistor_2_node));
  Adder adder_1 (
    .a(register_1_q), .b(pull_resistor_1_node), .out(adder_1_out), .cin(pull_resistor_2_node));  // open: cout
  RAM ram_1 (.addr(register_1_q), .data(ram_1_data), .clk(in_3), .ld(not_1_out));  // open: sel, clr
  not not_1 (not_1_out, pull_resistor_3_node);
  Pull_Resistor pull_resistor_3 (.node(pull_resistor_3_node));
  Register register_1 (.D(multiplexer_1_out), .Q(register_1_q), .clk(in_4));  // open: en, clr
  Multiplexer #(.width(8), .disabled(0), .enable("false")) multiplexer_1 (
    .in0(adder_1_out), .in1(controlled_buffer_5_out), .out(multiplexer_1_out), .sel(or_1_out));
  assign controlled_buffer_1_out = not_1_out ? ram_1_data : 8'bz;  // Controlled_Buffer controlled_buffer_1
  assign ram_1_data = pull_resistor_3_node ? in_1 : 8'bz;  // Controlled_Buffer controlled_buffer_2
  Pull_Resistor pull_resistor_4 (.node(pull_resistor_4_node));
  assign pull_resistor_4_node = multiplexer_2_out[0] ? undriven : 8'bz;  // Controlled_Buffer ALU_Return
  assign pull_resistor_4_node = multiplexer_2_out[3] ? controlled_buffer_1_out : 8'bz;  // Controlled_Buffer controlled_buffer_3
  assign controlled_buffer_4_out = not_2_out ? controlled_buffer_1_out : 8'bz;  // Controlled_Buffer controlled_buffer_4
  not not_2 (not_2_out, multiplexer_2_out[3]);
  assign controlled_buffer_5_out = or_1_out ? controlled_buffer_1_out : 8'bz;  // Controlled_Buffer controlled_buffer_5
  or or_1 (or_1_out, multiplexer_2_out[1], pull_resistor_5_node);
  Register Instruktionsregister (.D(controlled_buffer_4_out), .Q(Instruktionsregister_q), .clk(in_2));  // open: en, clr
  Register Operatorregister ();  // open: D, en, Q, clk, clr
  Demultiplexer #(.select(3), .width(8), .enable("false")) demultiplexer_1 (
    .out0(demultiplexer_1_out0), .out1(demultiplexer_1_out1), .out2(demultiplexer_1_out2),
    .out3(demultiplexer_1_out3), .out4(demultiplexer_1_out4), .out5(demultiplexer_1_out5),
    .out6(demultiplexer_1_out6), .out7(demultiplexer_1_out7), .in(pull_resistor_4_node),
    .sel(Instruktionsregister_q[6:4]));
  Multiplexer #(.select(4), .width(32), .disabled(0), .enable("false")) multiplexer_2 (
    .in0(32'h1), .in1(32'h2), .in2(32'h4), .in3(32'h8), .out(multiplexer_2_out),
    .sel(Instruktionsregister_q[3:0]));  // open: in4, in5, in6, in7, in8, in9, in10, in11, in12, in13, in14, in15
  Register register_2 (.D(demultiplexer_1_out0), .Q(register_2_q), .clk(undriven_2));  // open: en, clr
  Register register_3 (.D(demultiplexer_1_out1), .Q(register_3_q), .clk(undriven_2));  // open: en, clr
  Register register_4 (.D(demultiplexer_1_out2), .Q(register_4_q), .clk(undriven_2));  // open: en, clr
  Register register_5 (.D(demultiplexer_1_out3), .Q(register_5_q), .clk(undriven_2));  // open: en, clr
  Pull_Resistor pull_resistor_5 (.node(pull_resistor_5_node));
  assign pull_resistor_5_node = multiplexer_2_out[4] ? ALUFLAG_A_B : 1'bz;  // Controlled_Buffer controlled_buffer_6
  Register register_6 (.D(demultiplexer_1_out4), .Q(register_6_q), .clk(undriven_2));  // open: en, clr
  Register register_7 (.D(demultiplexer_1_out5), .Q(register_7_q), .clk(undriven_2));  // open: en, clr
  Register register_8 (.D(demultiplexer_1_out6), .Q(register_8_q), .clk(undriven_2));  // open: en, clr
  Register register_9 (.D(demultiplexer_1_out7), .Q(register_9_q), .clk(undriven_2));  // open: en, clr
  Multiplexer #(.select(3), .width(8), .enable("false")) multiplexer_3 (
    .in0(register_2_q), .in1(register_3_q), .in2(register_4_q), .in3(register_5_q), .in4(register_6_q),
    .in5(register_7_q), .in6(register_8_q), .in7(register_9_q), .out(in_1));  // open: sel
  Register Speicherregister (.D(undriven_3), .Q(Speicherregister_q));  // open: en, clk, clr
  Pull_Resistor pull_resistor_6 (.node(ALUFLAG_A_B));

  // Notes on the sheet:
  //   spezielle anweisung
  //   64bit fehlt!!!
  //   Schreibflag
  //   "Adresspuffer"
  //   Datenflag
  //   alternativadresse kann nicht direkt aus speicher kommen!!!
  //   von ALU
  //   ALU DATA FLAG
  //   Befehlsdecoder
  //   ____
  //   ausarbeiten!
  //   Registerauswahl/Operator0
  //   Prozessorrelevante Flags und Anweisung zur Befehlsausfuehrung
  //   Datenregister
  //   jumpflag
  //   ??? Entweder ReturnRegister zu Speicher oder Registerauswahl
  //   Operator1
  //   ALUin 0
  //   ALUout
  //   zu ALU
  //   ALUin 1
  //   ALUreturn
endmodule

module Time_Management_Unit (
  input  preINS,
  input  postINS,
  input  DataFlag,
  input  Clocktrigger,
  output InsLoadRequest,
  output DatLoadRequest,
  output out_7
);

  wire and_1_out, comparator_1_gt, comparator_1_lt, not_1_out, not_2_out, or_1_out;

  Comparator #(.width(1), .mode("unsigned")) comparator_1 (
    .a(preINS), .b(postINS), .gt(comparator_1_gt), .lt(comparator_1_lt));  // open: eq
  or or_1 (or_1_out, comparator_1_gt, comparator_1_lt);
  and and_1 (and_1_out, or_1_out, not_1_out);
  not not_1 (not_1_out, DataFlag);
  and and_2 (DatLoadRequest, DataFlag, not_2_out);
  not not_2 (not_2_out, Clocktrigger);
  and and_3 (InsLoadRequest, and_1_out, not_2_out);

  assign out_7 = Clocktrigger;
endmodule

module test (
  input  I1,
  input  I2,
  input  in_3,
  output Q1,
  output Q2
);

  wire not_1_out;

  not not_1 (not_1_out, I2);
  and and_1 (Q1, I1, not_1_out);

  assign Q2 = I2;
endmodule

module test1 (
  input  INS,
  input  DAT,
  input  CLK,
  output INR,
  output DAR,
  output ADR
);

  wire and_1_out, not_1_out, not_2_out, not_3_out;

  not not_1 (not_1_out, DAT);
  not not_2 (not_2_out, CLK);
  and and_1 (and_1_out, INS, not_1_out);
  not not_3 (not_3_out, CLK);
  and and_2 (DAR, DAT, not_2_out);
  and and_3 (INR, and_1_out, not_3_out);

  assign ADR = CLK;
endmodule

module test2 (
  input  INS,
  input  DAT,
  input  CLK,
  input  [3:0] r0,
  input  [3:0] r1,
  input  in_6,
  output INR,
  output DAR,
  output ADR,
  output [3:0] out_10,
  output out_11
);

  wire and_2_out, and_3_out, and_4_out, and_5_out, and_6_out, and_7_out, nand_2_out, not_1_out, not_2_out,
       not_3_out, not_4_out, not_5_out;
  wire [3:0] nand_1_out, nand_4_out;

  not not_1 (not_1_out, DAT);
  not not_2 (not_2_out, INS);
  not not_3 (not_3_out, CLK);
  not not_4 (not_4_out, INS);
  not not_5 (not_5_out, DAT);
  and and_1 (INR, INS, not_1_out);
  and and_2 (and_2_out, not_2_out, DAT);
  and and_3 (and_3_out, DAT, not_3_out);
  and and_4 (and_4_out, not_4_out, not_5_out);
  and and_5 (and_5_out, INS, DAT);
  or or_1 (DAR, and_2_out, and_3_out);
  and and_6 (and_6_out, and_4_out, CLK);
  and and_7 (and_7_out, and_5_out, CLK);
  or or_2 (ADR, and_6_out, and_7_out);
  assign nand_1_out = ~(r0 & r1);  // NAND_Gate nand_1, 4 bits wide
  nand nand_2 (nand_2_out, in_6, in_6);
  nand nand_3 (out_11, nand_2_out, nand_2_out);
  assign nand_4_out = ~(r0 & nand_1_out);  // NAND_Gate nand_4, 4 bits wide
  assign out_10 = ~(nand_4_out & nand_1_out);  // NAND_Gate nand_5, 4 bits wide
endmodule
