// Logisim project quicktest27122020ControllerImplementation.circ as structural Verilog
module main (
  input  MEMREQUEST,
  input  CLK,
  input  RESET,
  input  [7:0] in_4,
  input  in_5,
  input  in_6,
  input  in_7,
  input  in_8,
  input  in_9,
  input  in_10
);

  wire comparator_1_eq, comparator_1_gt, comparator_1_lt, controlled_inverter_3_out, demultiplexer_2_out0,
       demultiplexer_2_out1, not_1_out, not_2_out, time_management_unit_1_clk_adr,
       time_management_unit_1_clk_ins, time_management_unit_1_clk_ld, time_management_unit_1_write, undriven,
       undriven_3;
  wire [1:0] undriven_2;
  wire [7:0] adder_1_out, adder_2_out, adder_3_out, controlled_inverter_1_out, demultiplexer_1_out0,
       demultiplexer_1_out1, multiplexer_1_out, multiplexer_2_out, multiplexer_3_out, multiplexer_4_out,
       multiplexer_5_out, multiplexer_6_out, multiplexer_7_out, ram_1_data, register_1_q, register_2_q,
       register_3_q, register_4_q, register_5_q, register_6_q;

  Adder adder_1 (.a(register_1_q), .b({8{1'b0}}), .out(adder_1_out), .cin(1'b1));  // open: cout
  Multiplexer #(.width(8), .enable("false")) multiplexer_1 (
    .in0(adder_1_out), .in1(multiplexer_7_out), .out(multiplexer_1_out), .sel(register_2_q[0]));
  assign controlled_inverter_1_out = not_1_out ? ~{8{1'b0}} : 8'bz;  // Controlled_Inverter controlled_inverter_1
  not not_1 (not_1_out, MEMREQUEST);
  Register register_1 (
    .D(multiplexer_1_out), .Q(register_1_q), .clk(controlled_inverter_3_out), .clr(RESET));  // open: en
  assign controlled_inverter_1_out = MEMREQUEST ? ~register_1_q : 8'bz;  // Controlled_Inverter controlled_inverter_2
  assign controlled_inverter_3_out = MEMREQUEST ? ~time_management_unit_1_clk_adr : 1'bz;  // Controlled_Inverter controlled_inverter_3
  not not_2 (not_2_out, time_management_unit_1_write);
  RAM #(.bus("asynch")) ram_1 (.addr(controlled_inverter_1_out), .data(ram_1_data), .ld(not_2_out));  // open: sel, clr
  Pull_Resistor pull_resistor_1 (.node(ram_1_data));
  assign ram_1_data = register_2_q[3] ? adder_2_out : 8'bz;  // Controlled_Buffer controlled_buffer_1
  Demultiplexer #(.width(8), .enable("false")) demultiplexer_1 (
    .out0(demultiplexer_1_out0), .out1(demultiplexer_1_out1), .in(multiplexer_2_out), .sel(undriven));
  Multiplexer #(.width(8), .enable("false")) multiplexer_2 (
    .in0(adder_2_out), .in1(ram_1_data), .out(multiplexer_2_out), .sel(register_2_q[4]));
  Register register_2 (.D(ram_1_data), .Q(register_2_q), .clk(time_management_unit_1_clk_ins));  // open: en, clr
  Time_Management_Unit time_management_unit_1 (
    .loadflag(register_2_q[7]), .aluflag(register_2_q[4]), .writeflag(register_2_q[2]),
    .CLK_INS(time_management_unit_1_clk_ins), .CLK_ADR(time_management_unit_1_clk_adr),
    .CLK_LD(time_management_unit_1_clk_ld), .WRITE(time_management_unit_1_write), .CLK(CLK), .RESET(RESET));
  Multiplexer #(.width(8), .enable("false")) multiplexer_3 (
    .in0(adder_3_out), .in1(in_4), .out(multiplexer_3_out), .sel(in_5));
  Demultiplexer demultiplexer_2 (
    .out0(demultiplexer_2_out0), .out1(demultiplexer_2_out1), .in(in_10), .sel(in_6), .en(in_9));
  Register register_3 (
    .D(demultiplexer_1_out0), .Q(register_3_q), .clk(time_management_unit_1_clk_ld));  // open: en, clr
  Register register_4 (
    .D(demultiplexer_1_out1), .Q(register_4_q), .clk(time_management_unit_1_clk_ld));  // open: en, clr
  Register register_5 (.D(multiplexer_3_out), .Q(register_5_q), .clk(demultiplexer_2_out0));  // open: en, clr
  Register register_6 (.D(multiplexer_3_out), .Q(register_6_q), .clk(demultiplexer_2_out1));  // open: en, clr
  Multiplexer #(.width(8), .enable("false")) multiplexer_4 (
    .in0(register_3_q), .in1(register_4_q), .out(multiplexer_4_out), .sel(register_2_q[6]));
  Multiplexer #(.width(8), .enable("false")) multiplexer_5 (
    .in0(register_5_q), .in1(register_6_q), .out(multiplexer_5_out), .sel(in_8));
  Multiplexer #(.width(8), .enable("false")) multiplexer_6 (
    .in0(register_5_q), .in1(register_6_q), .out(multiplexer_6_out), .sel(in_7));
  Multiplexer #(.width(8), .enable("false")) multiplexer_7 (
    .in0(register_3_q), .in1(register_4_q), .out(multiplexer_7_out), .sel(register_2_q[5]));
  Adder adder_2 (.a(multiplexer_7_out), .b(multiplexer_4_out), .out(adder_2_out));  // open: cin, cout
  Comparator comparator_1 (
    .a(multiplexer_7_out), .b(multiplexer_4_out), .gt(comparator_1_gt), .eq(comparator_1_eq),
    .lt(comparator_1_lt));
  Adder adder_3 (.a(multiplexer_5_out), .b(multiplexer_6_out), .out(adder_3_out));  // open: cin, cout
  Multiplexer #(.select(2)) multiplexer_8 (
    .in0(comparator_1_gt), .in1(comparator_1_eq), .in2(comparator_1_lt), .sel(undriven_2), .en(undriven_3));  // open: in3, out

  // Notes on the sheet:
  //   ADRESSBUS
  //   CONTROLLER
  //   für jeden controller 1 Adresse
  //   ADD IPC somewhere here
  //   FESTWERTADRESSE
  //   JUMP Flag
  //   MEMREQUEST of Controller deactivates CLOCK of CPU
  //   WRITE Flag
  //   DATABUS
  //   WRITE Flag
  //   ALU Return Flag
  //   DEST
  //   DEST
  //   DEMUX (for design with small memory width) here?
  //   SRC0
  //   SRC1
  //   SRC0
  //   SRC1
  //   ALU
  //   ALU
  //   what holds the state of the ALU? -> Insert FlipFlop here somewhere
endmodule

module Time_Management_Unit (
  input  loadflag,
  input  aluflag,
  input  writeflag,
  input  CLK,
  input  RESET,
  output CLK_INS,
  output CLK_ADR,
  output CLK_LD,
  output WRITE
);

  wire demultiplexer_1_out0, demultiplexer_1_out2, demultiplexer_1_out3, not_1_out, or_1_out, register_1_q,
       register_3_q, xor_1_out;
  wire [1:0] counter_1_q;

  xor xor_1 (xor_1_out, CLK_LD, CLK_INS);
  or or_1 (or_1_out, loadflag, aluflag);
  Register #(.width(1)) register_1 (.D(or_1_out), .Q(register_1_q), .clk(xor_1_out));  // open: en, clr
  Register #(.width(1)) register_2 (.clk(xor_1_out));  // open: D, en, Q, clr
  Register #(.width(1)) register_3 (.D(writeflag), .Q(register_3_q), .clk(xor_1_out));  // open: en, clr
  Counter #(.width(2), .max('h3)) counter_1 (.Q(counter_1_q), .clk(CLK), .clr(RESET));  // open: load, D, count, carry
  Demultiplexer #(.select(2), .enable("false")) demultiplexer_1 (
    .out0(demultiplexer_1_out0), .out1(CLK_ADR), .out2(demultiplexer_1_out2), .out3(demultiplexer_1_out3),
    .in(1'b1), .sel(counter_1_q));
  and and_1 (CLK_INS, not_1_out, demultiplexer_1_out0);
  not not_1 (not_1_out, register_1_q);
  D_Flip_Flop d_ff_1 (
    .clk(CLK_ADR), .D(register_3_q), .Q(WRITE), .reset(demultiplexer_1_out3));  // open: Qn, preset, en
  and and_2 (CLK_LD, register_1_q, demultiplexer_1_out2);
endmodule

module neu (
  input  A,
  input  LF,
  output OUT
);

  wire not_1_out;

  not not_1 (not_1_out, LF);
  and and_1 (OUT, A, not_1_out);
endmodule

module TMUwithFLIPFLOP (
  input  loadflag,
  input  aluflag,
  input  writeflag,
  input  CLK,
  input  RESET,
  output CLK_INS,
  output CLK_ADR,
  output CLK_LD,
  output WRITE
);

  wire d_ff_1_q, d_ff_2_q, demultiplexer_1_out0, demultiplexer_1_out2, demultiplexer_1_out3, not_1_out,
       or_1_out, xor_1_out;
  wire [1:0] counter_1_q;

  xor xor_1 (xor_1_out, CLK_LD, CLK_INS);
  or or_1 (or_1_out, loadflag, aluflag);
  D_Flip_Flop d_ff_1 (.clk(xor_1_out), .D(or_1_out), .Q(d_ff_1_q));  // open: Qn, preset, en, reset
  D_Flip_Flop d_ff_2 (.clk(xor_1_out), .D(writeflag), .Q(d_ff_2_q));  // open: Qn, preset, en, reset
  Demultiplexer #(.select(2), .enable("false")) demultiplexer_1 (
    .out0(demultiplexer_1_out0), .out1(CLK_ADR), .out2(demultiplexer_1_out2), .out3(demultiplexer_1_out3),
    .in(1'b1), .sel(counter_1_q));
  Counter #(.width(2), .max('h3)) counter_1 (.Q(counter_1_q), .clk(CLK), .clr(RESET));  // open: load, D, count, carry
  and and_1 (CLK_INS, not_1_out, demultiplexer_1_out0);
  not not_1 (not_1_out, d_ff_1_q);
  D_Flip_Flop d_ff_3 (.clk(CLK_ADR), .D(d_ff_2_q), .Q(WRITE), .reset(demultiplexer_1_out3));  // open: Qn, preset, en
  and and_2 (CLK_LD, d_ff_1_q, demultiplexer_1_out2);

  // Notes on the sheet:
  //   Counter als IC
endmodule

module CD4051MUX (
  input  VDD,
  input  VEE,
  input  VSS,
  input  Ch0,
  input  Ch1,
  input  Ch2,
  input  Ch3,
  input  Ch4,
  input  Ch5,
  input  Ch6,
  input  Ch7,
  input  INH,
  input  A,
  input  B,
  input  C,
  output COM
);

  wire not_1_out;

  Multiplexer #(.select(3)) multiplexer_1 (
    .in0(Ch0), .in1(Ch1), .in2(Ch2), .in3(Ch3), .in4(Ch4), .in5(Ch5), .in6(Ch6), .in7(Ch7), .out(COM),
    .sel({C, B, A}), .en(not_1_out));
  not not_1 (not_1_out, INH);
endmodule

module CD4051DMX (
  input  VDD,
  input  VEE,
  input  VSS,
  input  COM,
  input  INH,
  input  A,
  input  B,
  input  C,
  output Ch0,
  output Ch1,
  output Ch2,
  output Ch3,
  output Ch4,
  output Ch5,
  output Ch6,
  output Ch7
);

  wire not_1_out;

  Demultiplexer #(.select(3)) demultiplexer_1 (
    .out0(Ch0), .out1(Ch1), .out2(Ch2), .out3(Ch3), .out4(Ch4), .out5(Ch5), .out6(Ch6), .out7(Ch7), .in(COM),
    .sel({C, B, A}), .en(not_1_out));
  not not_1 (not_1_out, INH);
  Pull_Resistor pull_resistor_1 (.node(A));
  Pull_Resistor pull_resistor_2 (.node(B));
  Pull_Resistor pull_resistor_3 (.node(C));
endmodule

module CD4013 (
  input  VDD,
  input  VSS,
  input  CLOCK1,
  input  D1,
  input  SET1,
  input  RESET1,
  input  CLOCK2,
  input  D2,
  input  SET2,
  input  RESET2,
  output Q1,
  output nQ1,
  output Q2,
  output nQ2
);

  D_Flip_Flop d_ff_1 (.clk(CLOCK1), .D(D1), .Q(Q1), .Qn(nQ1), .preset(SET1), .reset(RESET1));  // open: en
  D_Flip_Flop d_ff_2 (.clk(CLOCK2), .D(D2), .Q(Q2), .Qn(nQ2), .preset(SET2), .reset(RESET2));  // open: en
endmodule

module CD4585 (
  input  VDD,
  input  VSS,
  input  A_B_In,
  input  A_B_In_2,
  input  A_B_In_3,
  input  A0,
  input  A1,
  input  A2,
  input  A3,
  input  B0,
  input  B1,
  input  B2,
  input  B3,
  output A_B_Out,
  output A_B_Out_2,
  output A_B_Out_3
);

  Comparator #(.width(4), .mode("unsigned")) comparator_1 (
    .a({A3, A2, A1, A0}), .b({B3, B2, B1, B0}), .gt(A_B_Out), .eq(A_B_Out_2), .lt(A_B_Out_3));
endmodule

module Group1 (
  input  in_1
);

  wire cd4013_1_nq1, cd4013_1_nq2, cd4013_2_nq1, undriven;

  CD4013 cd4013_1 (
    .D1(cd4013_1_nq1), .CLOCK2(cd4013_1_nq1), .nQ1(cd4013_1_nq1), .nQ2(cd4013_1_nq2), .SET1(in_1));  // open: VDD, VSS, CLOCK1, D2, Q1, Q2, SET2, RESET1, RESET2
  CD4013 cd4013_2 (
    .CLOCK1(cd4013_1_nq2), .D1(undriven), .CLOCK2(cd4013_2_nq1), .nQ1(cd4013_2_nq1));  // open: VDD, VSS, D2, Q1, Q2, nQ2, SET1, SET2, RESET1, RESET2
endmodule

module Group3 (
  input  in_1,
  input  in_2,
  input  in_3,
  input  in_4,
  input  in_5,
  input  [3:0] in_6
);

  wire cd4013_1_q1, cd4013_1_q2, cd4013_2_q1, cd4013_2_q2, cd4013_3_q2, cd4013_4_q2, cd4013_5_q1,
       cd4013_5_q2, cd4013_6_q1, cd4013_6_q2, cd4013_7_q2, cd4013_8_q2, cd4013_9_q1, cd4013_9_q2,
       cd4013_10_q1, cd4013_10_q2, cd4013_11_q2, cd4013_12_q2, cd4013_13_q1, cd4013_13_q2, cd4013_14_q1,
       cd4013_14_q2, cd4013_15_q2, cd4013_16_q2, cd4051dmx_1_ch0, cd4051dmx_1_ch1, cd4051dmx_1_ch2,
       cd4051dmx_1_ch3, cd4051dmx_1_ch4, cd4051dmx_1_ch5, cd4051dmx_1_ch6, cd4051dmx_1_ch7;

  CD4051DMX cd4051dmx_1 (
    .COM(in_1), .Ch0(cd4051dmx_1_ch0), .Ch1(cd4051dmx_1_ch1), .Ch2(cd4051dmx_1_ch2), .Ch3(cd4051dmx_1_ch3),
    .Ch4(cd4051dmx_1_ch4), .Ch5(cd4051dmx_1_ch5), .Ch6(cd4051dmx_1_ch6), .Ch7(cd4051dmx_1_ch7), .INH(in_2),
    .C(in_5), .B(in_4), .A(in_3));  // open: VDD, VSS, VEE
  CD4013 cd4013_1 (
    .CLOCK1(cd4051dmx_1_ch0), .D1(in_6[3]), .CLOCK2(cd4051dmx_1_ch0), .D2(in_6[2]), .Q1(cd4013_1_q1),
    .Q2(cd4013_1_q2));  // open: VDD, VSS, nQ1, nQ2, SET1, SET2, RESET1, RESET2
  CD4013 cd4013_2 (
    .CLOCK1(cd4051dmx_1_ch1), .D1(in_6[3]), .CLOCK2(cd4051dmx_1_ch1), .D2(in_6[2]), .Q1(cd4013_2_q1),
    .Q2(cd4013_2_q2));  // open: VDD, VSS, nQ1, nQ2, SET1, SET2, RESET1, RESET2
  CD4013 cd4013_3 (
    .CLOCK1(cd4051dmx_1_ch2), .D1(in_6[3]), .CLOCK2(cd4051dmx_1_ch2), .D2(in_6[2]), .Q2(cd4013_3_q2));  // open: VDD, VSS, Q1, nQ1, nQ2, SET1, SET2, RESET1, RESET2
  CD4013 cd4013_4 (
    .CLOCK1(cd4051dmx_1_ch3), .D1(in_6[3]), .CLOCK2(cd4051dmx_1_ch3), .D2(in_6[2]), .Q2(cd4013_4_q2));  // open: VDD, VSS, Q1, nQ1, nQ2, SET1, SET2, RESET1, RESET2
  CD4013 cd4013_5 (
    .CLOCK1(cd4051dmx_1_ch4), .D1(in_6[3]), .CLOCK2(cd4051dmx_1_ch4), .D2(in_6[2]), .Q1(cd4013_5_q1),
    .Q2(cd4013_5_q2));  // open: VDD, VSS, nQ1, nQ2, SET1, SET2, RESET1, RESET2
  CD4013 cd4013_6 (
    .CLOCK1(cd4051dmx_1_ch5), .D1(in_6[3]), .CLOCK2(cd4051dmx_1_ch5), .D2(in_6[2]), .Q1(cd4013_6_q1),
    .Q2(cd4013_6_q2));  // open: VDD, VSS, nQ1, nQ2, SET1, SET2, RESET1, RESET2
  CD4013 cd4013_7 (
    .CLOCK1(cd4051dmx_1_ch6), .D1(in_6[3]), .CLOCK2(cd4051dmx_1_ch6), .D2(in_6[2]), .Q2(cd4013_7_q2));  // open: VDD, VSS, Q1, nQ1, nQ2, SET1, SET2, RESET1, RESET2
  CD4013 cd4013_8 (
    .CLOCK1(cd4051dmx_1_ch7), .D1(in_6[3]), .CLOCK2(cd4051dmx_1_ch7), .D2(in_6[2]), .Q2(cd4013_8_q2));  // open: VDD, VSS, Q1, nQ1, nQ2, SET1, SET2, RESET1, RESET2
  CD4013 cd4013_9 (
    .CLOCK1(cd4051dmx_1_ch0), .D1(in_6[1]), .CLOCK2(cd4051dmx_1_ch0), .D2(in_6[0]), .Q1(cd4013_9_q1),
    .Q2(cd4013_9_q2));  // open: VDD, VSS, nQ1, nQ2, SET1, SET2, RESET1, RESET2
  CD4013 cd4013_10 (
    .CLOCK1(cd4051dmx_1_ch1), .D1(in_6[1]), .CLOCK2(cd4051dmx_1_ch1), .D2(in_6[0]), .Q1(cd4013_10_q1),
    .Q2(cd4013_10_q2));  // open: VDD, VSS, nQ1, nQ2, SET1, SET2, RESET1, RESET2
  CD4013 cd4013_11 (
    .CLOCK1(cd4051dmx_1_ch2), .D1(in_6[1]), .CLOCK2(cd4051dmx_1_ch2), .D2(in_6[0]), .Q2(cd4013_11_q2));  // open: VDD, VSS, Q1, nQ1, nQ2, SET1, SET2, RESET1, RESET2
  CD4013 cd4013_12 (
    .CLOCK1(cd4051dmx_1_ch3), .D1(in_6[1]), .CLOCK2(cd4051dmx_1_ch3), .D2(in_6[0]), .Q2(cd4013_12_q2));  // open: VDD, VSS, Q1, nQ1, nQ2, SET1, SET2, RESET1, RESET2
  CD4013 cd4013_13 (
    .CLOCK1(cd4051dmx_1_ch4), .D1(in_6[1]), .CLOCK2(cd4051dmx_1_ch4), .D2(in_6[0]), .Q1(cd4013_13_q1),
    .Q2(cd4013_13_q2));  // open: VDD, VSS, nQ1, nQ2, SET1, SET2, RESET1, RESET2
  CD4013 cd4013_14 (
    .CLOCK1(cd4051dmx_1_ch5), .D1(in_6[1]), .CLOCK2(cd4051dmx_1_ch5), .D2(in_6[0]), .Q1(cd4013_14_q1),
    .Q2(cd4013_14_q2));  // open: VDD, VSS, nQ1, nQ2, SET1, SET2, RESET1, RESET2
  CD4013 cd4013_15 (
    .CLOCK1(cd4051dmx_1_ch6), .D1(in_6[1]), .CLOCK2(cd4051dmx_1_ch6), .D2(in_6[0]), .Q2(cd4013_15_q2));  // open: VDD, VSS, Q1, nQ1, nQ2, SET1, SET2, RESET1, RESET2
  CD4013 cd4013_16 (
    .CLOCK1(cd4051dmx_1_ch7), .D1(in_6[1]), .CLOCK2(cd4051dmx_1_ch7), .D2(in_6[0]), .Q2(cd4013_16_q2));  // open: VDD, VSS, Q1, nQ1, nQ2, SET1, SET2, RESET1, RESET2

  // Notes on the sheet:
  //   coming from INSREG
endmodule

module Group4 (
  input  [3:0] in_1,
  input  [3:0] in_2,
  input  [3:0] in_3,
  input  [3:0] in_4,
  input  [3:0] in_5,
  input  [3:0] in_6,
  input  [3:0] in_7,
  input  [3:0] in_8,
  input  in_9,
  input  in_10,
  input  in_11,
  input  in_12,
  input  in_13,
  input  in_14,
  input  in_15
);

  wire cd4051mux_1_com, cd4051mux_2_com, cd4051mux_3_com, cd4051mux_4_com;

  CD4051MUX cd4051mux_1 (
    .COM(cd4051mux_1_com), .Ch0(in_1[0]), .Ch1(in_2[0]), .Ch2(in_3[0]), .Ch3(in_4[0]), .Ch4(in_5[0]),
    .Ch5(in_6[0]), .Ch6(in_7[0]), .Ch7(in_8[0]), .INH(in_9), .C(in_13), .B(in_14), .A(in_15));  // open: VDD, VEE, VSS
  CD4051MUX cd4051mux_2 (
    .COM(cd4051mux_2_com), .Ch0(in_1[2]), .Ch1(in_2[2]), .Ch2(in_3[2]), .Ch3(in_4[2]), .Ch4(in_5[2]),
    .Ch5(in_6[2]), .Ch6(in_7[2]), .Ch7(in_8[2]), .INH(in_9), .C(in_13), .B(in_14), .A(in_15));  // open: VDD, VEE, VSS
  CD4051MUX cd4051mux_3 (
    .COM(cd4051mux_3_com), .Ch0(in_1[1]), .Ch1(in_2[1]), .Ch2(in_3[1]), .Ch3(in_4[1]), .Ch4(in_5[1]),
    .Ch5(in_6[1]), .Ch6(in_7[1]), .Ch7(in_8[1]), .INH(in_9), .C(in_13), .B(in_14), .A(in_15));  // open: VDD, VEE, VSS
  CD4051MUX cd4051mux_4 (
    .COM(cd4051mux_4_com), .Ch0(in_1[3]), .Ch1(in_2[3]), .Ch2(in_3[3]), .Ch3(in_4[3]), .Ch4(in_5[3]),
    .Ch5(in_6[3]), .Ch6(in_7[3]), .Ch7(in_8[3]), .INH(in_9), .C(in_13), .B(in_14), .A(in_15));  // open: VDD, VEE, VSS

  // Notes on the sheet:
  //   ALU In0
endmodule

module Group5 (
  input  [3:0] in_1,
  input  [3:0] in_2,
  input  in_3,
  input  in_4,
  input  in_5,
  input  in_6
);

  wire cd4051mux_1_com, cd4585_1_a_b_out, cd4585_1_a_b_out_2, cd4585_1_a_b_out_3;

  CD4585 cd4585_1 (
    .A0(in_1[0]), .A1(in_1[1]), .A2(in_1[2]), .A3(in_1[3]), .B0(in_2[0]), .B1(in_2[1]), .B2(in_2[2]),
    .B3(in_2[3]), .A_B_Out(cd4585_1_a_b_out), .A_B_Out_2(cd4585_1_a_b_out_2), .A_B_Out_3(cd4585_1_a_b_out_3));  // open: VDD, VSS, A_B_In, A_B_In_2, A_B_In_3
  CD4051MUX cd4051mux_1 (
    .COM(cd4051mux_1_com), .Ch0(cd4585_1_a_b_out_3), .Ch1(cd4585_1_a_b_out), .Ch2(cd4585_1_a_b_out_2),
    .INH(in_3), .C(in_6), .B(in_5), .A(in_4));  // open: VDD, VEE, VSS, Ch3, Ch4, Ch5, Ch6, Ch7

  // Notes on the sheet:
  //   JUMPFLAG
endmodule

module Group6 (
  input  CLOCK
);

  wire cd4013_1_nq1, cd4013_1_nq2, cd4013_1_q1, cd4013_1_q2, pull_resistor_1_node, pull_resistor_2_node;

  Pull_Resistor #(.pull(1)) pull_resistor_1 (.node(pull_resistor_1_node));
  Pull_Resistor pull_resistor_2 (.node(pull_resistor_2_node));
  CD4051DMX cd4051dmx_1 (
    .COM(pull_resistor_1_node), .INH(pull_resistor_2_node), .B(cd4013_1_q2), .A(cd4013_1_q1));  // open: Ch0, Ch1, Ch2, Ch3, Ch4, Ch5, Ch6, Ch7, C, VDD, VSS, VEE
  CD4013 cd4013_1 (
    .CLOCK1(CLOCK), .D1(cd4013_1_nq1), .CLOCK2(cd4013_1_nq1), .D2(cd4013_1_nq2), .Q1(cd4013_1_q1),
    .nQ1(cd4013_1_nq1), .Q2(cd4013_1_q2), .nQ2(cd4013_1_nq2));  // open: VDD, VSS, SET1, SET2, RESET1, RESET2
endmodule

module CD4071 (
);

  // OR_Gate or_1 is placed but not wired
  // OR_Gate or_2 is placed but not wired
  // OR_Gate or_3 is placed but not wired
  // OR_Gate or_4 is placed but not wired
endmodule

module mem (
);

  wire [7:0] ram_1_data;

  RAM ram_1 (.data(ram_1_data));  // open: addr, sel, clk, ld, clr

  // Notes on the sheet:
  //   CONTROLLER
  //   CPU
endmodule
